# Fritzing sketch led_strip_bling_bling (saved by Fritzing 0.9.2b)
circuit board: 1.30046cm x 2.30299cm
breadboards: 1

parts:
  U1 = attiny85 [package=dip]
  J2 = male pin header, 3 pins [form="♂ (male)"]
  S1 = Pushbutton [package="[THT]"]
  J3 = male pin header, 3 pins [form="♂ (male)"]

nets:
  N1: U1.Pin_2, S1.Pin_3, S1.Pin_4
  N2: U1.Pin_3, J2.pin3
  N3: U1.Pin_4, U1.Pin_5, J2.pin1, S1.Pin_1, S1.Pin_2, J3.pin3
  N4: U1.Pin_6, U1.Pin_8, J2.pin2, J3.pin2
  N5: U1.Pin_7, J3.pin1

notes:
  -
  +
  +5V
  GND
  DATA IN
  RC
  S
  out
